// Logisim project CPU.circ as structural Verilog: 6 circuits, main circuit Processor
module Processor (
);

  wire ALU_EQ, ALU_GT, ALU_GTU, ALU_LT, ALU_LTU, ALU_RDY, and_1_out, and_2_out, and_3_out, and_4_out,
       and_5_out, and_6_out, BM0, BM1, BM2, BM3, button_1_out, CLK, EALIGN, FETCH, INT, JMP, LOAD0, LOAD1,
       loadstoreunit_1_ealign, loadstoreunit_1_nrw, loadstoreunit_1_strobe, multiplexer_4_out, not_1_out,
       not_2_out, not_3_out, OPIMM, or_1_out, PCE, PCREL, programcounter_1_ealign, REG_WE, RST, SIGILL, SLT,
       SLTU, STORE0, STORE1;
  wire [3:0] ALU_OP;
  wire [4:0] WI, XI, YI;
  wire [15:0] loadstoreunit_1_a;
  wire [29:16] loadstoreunit_1_a_2;
  wire [31:0] ALU_R, bit_extender_1_out, IMM, INSTR, LSU_IN, multiplexer_1_out, multiplexer_2_out,
       multiplexer_3_out, MUX_R, PC, ram_1_data, REG_X, REG_Y, register_1_q, register_2_q, rom_1_data;

  and and_1 (and_1_out, 1'b1, loadstoreunit_1_a_2[29], loadstoreunit_1_a_2[28], loadstoreunit_1_a_2[27], loadstoreunit_1_a_2[26], loadstoreunit_1_a_2[25], loadstoreunit_1_a_2[24], loadstoreunit_1_a_2[23], loadstoreunit_1_a_2[22], loadstoreunit_1_a_2[21], loadstoreunit_1_a_2[20], loadstoreunit_1_a_2[19], loadstoreunit_1_a_2[18], loadstoreunit_1_a_2[17], loadstoreunit_1_a_2[16]);
  not not_1 (not_1_out, and_1_out);
  not not_2 (not_2_out, not_3_out);
  ROM #(.addrWidth(16), .dataWidth(32)) rom_1 (.addr(loadstoreunit_1_a), .data(rom_1_data));
  RAM #(.addrWidth(16), .asyncread("true"), .dataWidth(32), .databus("bidir")) ram_1 (
    .addr(loadstoreunit_1_a), .we(and_2_out), .oe(and_3_out), .clk(loadstoreunit_1_strobe), .data(ram_1_data));
  and and_2 (and_2_out, not_2_out, not_1_out);
  and and_3 (and_3_out, not_1_out, not_3_out);
  // Probe on {loadstoreunit_1_a_2, loadstoreunit_1_a}
  Register #(.width(32)) register_1 (.D(rom_1_data), .clk(and_4_out), .Q(register_1_q));  // open: en, clr
  and and_4 (and_4_out, and_1_out, loadstoreunit_1_strobe);
  and and_5 (and_5_out, and_1_out, not_3_out);
  assign ram_1_data = and_5_out ? register_1_q : 32'bz;  // Controlled_Buffer controlled_buffer_1
  // Probe on ram_1_data
  not not_3 (not_3_out, loadstoreunit_1_nrw);
  or or_1 (or_1_out, LOAD1, LOAD0);
  Multiplexer #(.width(32)) multiplexer_1 (.in0(MUX_R), .in1(LSU_IN), .out(multiplexer_1_out), .sel(or_1_out));
  LoadStoreUnit loadstoreunit_1 (
    .DIN(LSU_IN), .DO(ram_1_data), .INSTR(INSTR), .PCE(PCE), .A({loadstoreunit_1_a_2, loadstoreunit_1_a}),
    .STROBE(loadstoreunit_1_strobe), .EALIGN(loadstoreunit_1_ealign), .BM0(BM0), .BM1(BM1), .BM2(BM2),
    .BM3(BM3), .nRW(loadstoreunit_1_nrw), .nBUSY(1'b1), .CLK(CLK), .RST(RST), .FETCH(FETCH), .LOAD0(LOAD0),
    .LOAD1(LOAD1), .STORE0(STORE0), .STORE1(STORE1), .ADDR(ALU_R), .PC(PC), .DI(ram_1_data), .DOUT(REG_Y));  // open: RDY
  ProgramCounter programcounter_1 (
    .PC(PC), .EALIGN(programcounter_1_ealign), .ADDR(MUX_R), .RST(RST), .INT(INT), .JMP(JMP), .PCE(PCE),
    .CLK(CLK));
  // Probe on multiplexer_1_out
  RegisterFile registerfile_1 (.Y(REG_Y), .X(REG_X), .YI(YI), .D(multiplexer_1_out), .WI(WI), .WR(and_6_out), .XI(XI));
  and and_6 (and_6_out, REG_WE, CLK);
  or or_2 (EALIGN, loadstoreunit_1_ealign, programcounter_1_ealign);
  Register #(.trigger("falling"), .width(32)) register_2 (.D(INSTR), .clk(CLK), .Q(register_2_q));  // open: en, clr
  InstructionDecoder instructiondecoder_1 (.IMM(IMM), .SIGILL(SIGILL), .INSTR(register_2_q));
  ArithmeticLogicUnit arithmeticlogicunit_1 (
    .R(ALU_R), .RDY(ALU_RDY), .EQ(ALU_EQ), .LT(ALU_LT), .GT(ALU_GT), .LTU(ALU_LTU), .GTU(ALU_GTU),
    .SEL(ALU_OP), .X(multiplexer_2_out), .Y(multiplexer_3_out), .CLK(CLK));
  Multiplexer #(.width(32)) multiplexer_2 (.in0(REG_X), .in1(PC), .out(multiplexer_2_out), .sel(PCREL));
  Multiplexer #(.width(32)) multiplexer_3 (.in0(REG_Y), .in1(IMM), .out(multiplexer_3_out), .sel(OPIMM));
  assign bit_extender_1_out = {{31{multiplexer_4_out}}, multiplexer_4_out};  // Bit_Extender bit_extender_1
  Multiplexer multiplexer_4 (.in0(ALU_LT), .in1(ALU_LTU), .out(multiplexer_4_out), .sel(SLTU));
  Multiplexer #(.width(32)) multiplexer_5 (.in0(ALU_R), .in1(bit_extender_1_out), .out(MUX_R), .sel(SLT));
  // Probe on MUX_R
  LED led_1 (.in(SIGILL));
  // Probe on IMM
  T_Flip_Flop t_ff_1 (.T(1'b1), .clk(button_1_out), .Q(CLK));  // open: Qn, reset, preset
  Button button_1 (.out(button_1_out));
  DipSwitch #(.number(14)) dipswitch_1 (
    .sw1(RST), .sw2(FETCH), .sw3(JMP), .sw4(INT), .sw5(PCREL), .sw6(OPIMM), .sw7(REG_WE), .sw8(SLT),
    .sw9(SLTU), .sw10(LOAD0), .sw11(LOAD1), .sw12(STORE0), .sw13(STORE1));  // open: sw14
  Slider #(.width(5)) slider_1 (.out(WI));
  Slider #(.width(5)) slider_2 (.out(XI));
  Slider #(.width(5)) slider_3 (.out(YI));
  Slider #(.width(4)) slider_4 (.out(ALU_OP));

  // Notes on the sheet:
  //   contents of rom_1 (hex, n*v repeats v):
  //   fe010113 812e23 2010413 17b7 23478793 fef42623 fec42703 27b7 34478793 e7e863 fec42783 a78793
  //   fef42623 fec42703 8abcd7b7 f707b3 78713 fec42783 ab78793 f72023 fec42783 178793 fef42623 fbdff06f
  //   65508*0 10000113 fffc00b7 8067 10000113
endmodule

module RegisterFile (
  input  [4:0] WI,
  input  WR,
  input  [31:0] D,
  input  [4:0] XI,
  input  [4:0] YI,
  output [31:0] X,
  output [31:0] Y
);

  wire W1, W2, W3, W4, W5, W6, W7, W8, W9, W10, W11, W12, W13, W14, W15, W16, W17, W18, W19, W20, W21, W22,
       W23, W24, W25, W26, W27, W28, W29, W30, W31;
  wire [0:0] decoder_1_out0;
  wire [31:0] R1, R2, R3, R4, R5, R6, R7, R8, R9, R10, R11, R12, R13, R14, R15, R16, R17, R18, R19, R20, R21,
       R22, R23, R24, R25, R26, R27, R28, R29, R30, R31;

  Register #(.width(32)) register_1 (.D(D), .clk(W1), .Q(R1));  // open: en, clr
  Register #(.width(32)) register_2 (.D(D), .clk(W2), .Q(R2));  // open: en, clr
  Register #(.width(32)) register_3 (.D(D), .clk(W3), .Q(R3));  // open: en, clr
  // NoConnect on decoder_1_out0[0]
  Register #(.width(32)) register_4 (.D(D), .clk(W4), .Q(R4));  // open: en, clr
  Register #(.width(32)) register_5 (.D(D), .clk(W5), .Q(R5));  // open: en, clr
  Register #(.width(32)) register_6 (.D(D), .clk(W6), .Q(R6));  // open: en, clr
  Register #(.width(32)) register_7 (.D(D), .clk(W7), .Q(R7));  // open: en, clr
  Decoder #(.select(5)) decoder_1 (
    .out0(decoder_1_out0[0]), .out1(W1), .out2(W2), .out3(W3), .out4(W4), .out5(W5), .out6(W6), .out7(W7),
    .out8(W8), .out9(W9), .out10(W10), .out11(W11), .out12(W12), .out13(W13), .out14(W14), .out15(W15),
    .out16(W16), .out17(W17), .out18(W18), .out19(W19), .out20(W20), .out21(W21), .out22(W22), .out23(W23),
    .out24(W24), .out25(W25), .out26(W26), .out27(W27), .out28(W28), .out29(W29), .out30(W30), .out31(W31),
    .sel(WI), .en(WR));
  Register #(.width(32)) register_8 (.D(D), .clk(W8), .Q(R8));  // open: en, clr
  Register #(.width(32)) register_9 (.D(D), .clk(W9), .Q(R9));  // open: en, clr
  Register #(.width(32)) register_10 (.D(D), .clk(W10), .Q(R10));  // open: en, clr
  Register #(.width(32)) register_11 (.D(D), .clk(W11), .Q(R11));  // open: en, clr
  Register #(.width(32)) register_12 (.D(D), .clk(W12), .Q(R12));  // open: en, clr
  Register #(.width(32)) register_13 (.D(D), .clk(W13), .Q(R13));  // open: en, clr
  Register #(.width(32)) register_14 (.D(D), .clk(W14), .Q(R14));  // open: en, clr
  Register #(.width(32)) register_15 (.D(D), .clk(W15), .Q(R15));  // open: en, clr
  Multiplexer #(.select(5), .width(32)) multiplexer_1 (
    .in0({32{1'b0}}), .in1(R1), .in2(R2), .in3(R3), .in4(R4), .in5(R5), .in6(R6), .in7(R7), .in8(R8),
    .in9(R9), .in10(R10), .in11(R11), .in12(R12), .in13(R13), .in14(R14), .in15(R15), .in16(R16), .in17(R17),
    .in18(R18), .in19(R19), .in20(R20), .in21(R21), .in22(R22), .in23(R23), .in24(R24), .in25(R25),
    .in26(R26), .in27(R27), .in28(R28), .in29(R29), .in30(R30), .in31(R31), .out(X), .sel(XI));
  Register #(.width(32)) register_16 (.D(D), .clk(W16), .Q(R16));  // open: en, clr
  Register #(.width(32)) register_17 (.D(D), .clk(W17), .Q(R17));  // open: en, clr
  Register #(.width(32)) register_18 (.D(D), .clk(W18), .Q(R18));  // open: en, clr
  Register #(.width(32)) register_19 (.D(D), .clk(W19), .Q(R19));  // open: en, clr
  Register #(.width(32)) register_20 (.D(D), .clk(W20), .Q(R20));  // open: en, clr
  Register #(.width(32)) register_21 (.D(D), .clk(W21), .Q(R21));  // open: en, clr
  Register #(.width(32)) register_22 (.D(D), .clk(W22), .Q(R22));  // open: en, clr
  Register #(.width(32)) register_23 (.D(D), .clk(W23), .Q(R23));  // open: en, clr
  Register #(.width(32)) register_24 (.D(D), .clk(W24), .Q(R24));  // open: en, clr
  Register #(.width(32)) register_25 (.D(D), .clk(W25), .Q(R25));  // open: en, clr
  Register #(.width(32)) register_26 (.D(D), .clk(W26), .Q(R26));  // open: en, clr
  Register #(.width(32)) register_27 (.D(D), .clk(W27), .Q(R27));  // open: en, clr
  Multiplexer #(.select(5), .width(32)) multiplexer_2 (
    .in0({32{1'b0}}), .in1(R1), .in2(R2), .in3(R3), .in4(R4), .in5(R5), .in6(R6), .in7(R7), .in8(R8),
    .in9(R9), .in10(R10), .in11(R11), .in12(R12), .in13(R13), .in14(R14), .in15(R15), .in16(R16), .in17(R17),
    .in18(R18), .in19(R19), .in20(R20), .in21(R21), .in22(R22), .in23(R23), .in24(R24), .in25(R25),
    .in26(R26), .in27(R27), .in28(R28), .in29(R29), .in30(R30), .in31(R31), .out(Y), .sel(YI));
  Register #(.width(32)) register_28 (.D(D), .clk(W28), .Q(R28));  // open: en, clr
  Register #(.width(32)) register_29 (.D(D), .clk(W29), .Q(R29));  // open: en, clr
  Register #(.width(32)) register_30 (.D(D), .clk(W30), .Q(R30));  // open: en, clr
  Register #(.width(32)) register_31 (.D(D), .clk(W31), .Q(R31));  // open: en, clr

  // Other names for the same wires on the sheet: DI[31:0] = D
endmodule

module ProgramCounter (
  input  [31:0] ADDR,
  input  RST,
  input  INT,
  input  JMP,
  input  PCE,
  input  CLK,
  output [31:0] PC,
  output EALIGN
);

  wire n74161_1_pin1, n74161_1_pin5, n74161_1_pin6, n74161_1_pin7, n74161_1_pin9, n74161_1_pin10,
       n74161_2_pin7, n74161_2_pin10, n74161_3_pin1, n74161_3_pin7, n74161_3_pin10, n74161_4_pin1,
       n74161_4_pin7, n74161_4_pin10, n74161_5_pin1, n74161_5_pin7, n74161_5_pin10, n74161_6_pin1,
       n74161_6_pin7, n74161_6_pin10, n74161_7_pin1, n74161_7_pin7, n74161_7_pin10, n74161_8_pin1,
       n74161_8_pin7, or_1_out;
  wire [3:0] n74161_6_pin3;
  wire [29:0] multiplexer_1_out;

  _74161 #(.ShowInternalStructure("true")) u_74161_1 (
    .pin1(n74161_1_pin1), .pin2(CLK), .pin3(multiplexer_1_out[28]), .pin4(multiplexer_1_out[29]),
    .pin5(n74161_1_pin5), .pin6(n74161_1_pin6), .pin7(n74161_1_pin7), .pin14(PC[31]), .pin13(PC[30]),
    .pin10(n74161_1_pin10), .pin9(n74161_1_pin9));  // open: pin15, pin12, pin11
  _74161 #(.ShowInternalStructure("true")) u_74161_2 (
    .pin2(CLK), .pin3(multiplexer_1_out[24]), .pin4(multiplexer_1_out[25]), .pin5(multiplexer_1_out[26]),
    .pin6(multiplexer_1_out[27]), .pin7(n74161_2_pin7), .pin15(n74161_1_pin10), .pin14(PC[26]),
    .pin13(PC[27]), .pin12(PC[28]), .pin11(PC[29]), .pin10(n74161_2_pin10), .pin9(n74161_1_pin9));  // open: pin1
  _74161 #(.ShowInternalStructure("true")) u_74161_3 (
    .pin1(n74161_3_pin1), .pin2(CLK), .pin3(multiplexer_1_out[20]), .pin4(multiplexer_1_out[21]),
    .pin5(multiplexer_1_out[22]), .pin6(multiplexer_1_out[23]), .pin7(n74161_3_pin7), .pin15(n74161_2_pin10),
    .pin14(PC[22]), .pin13(PC[23]), .pin12(PC[24]), .pin11(PC[25]), .pin10(n74161_3_pin10),
    .pin9(n74161_1_pin9));
  _74161 #(.ShowInternalStructure("true")) u_74161_4 (
    .pin1(n74161_4_pin1), .pin2(CLK), .pin3(multiplexer_1_out[16]), .pin4(multiplexer_1_out[17]),
    .pin5(multiplexer_1_out[18]), .pin6(multiplexer_1_out[19]), .pin7(n74161_4_pin7), .pin15(n74161_3_pin10),
    .pin14(PC[18]), .pin13(PC[19]), .pin12(PC[20]), .pin11(PC[21]), .pin10(n74161_4_pin10),
    .pin9(n74161_1_pin9));
  _74161 #(.ShowInternalStructure("true")) u_74161_5 (
    .pin1(n74161_5_pin1), .pin2(CLK), .pin3(multiplexer_1_out[12]), .pin4(multiplexer_1_out[13]),
    .pin5(multiplexer_1_out[14]), .pin6(multiplexer_1_out[15]), .pin7(n74161_5_pin7), .pin15(n74161_4_pin10),
    .pin14(PC[14]), .pin13(PC[15]), .pin12(PC[16]), .pin11(PC[17]), .pin10(n74161_5_pin10),
    .pin9(n74161_1_pin9));
  _74161 #(.ShowInternalStructure("true")) u_74161_6 (
    .pin1(n74161_6_pin1), .pin2(CLK), .pin3(n74161_6_pin3[0]), .pin4(n74161_6_pin3[1]),
    .pin5(n74161_6_pin3[2]), .pin6(n74161_6_pin3[3]), .pin7(n74161_6_pin7), .pin15(n74161_5_pin10),
    .pin14(PC[10]), .pin13(PC[11]), .pin12(PC[12]), .pin11(PC[13]), .pin10(n74161_6_pin10),
    .pin9(n74161_1_pin9));
  _74161 #(.ShowInternalStructure("true")) u_74161_7 (
    .pin1(n74161_7_pin1), .pin2(CLK), .pin3(multiplexer_1_out[4]), .pin4(multiplexer_1_out[5]),
    .pin5(multiplexer_1_out[6]), .pin6(multiplexer_1_out[7]), .pin7(n74161_7_pin7), .pin15(n74161_6_pin10),
    .pin14(PC[6]), .pin13(PC[7]), .pin12(PC[8]), .pin11(PC[9]), .pin10(n74161_7_pin10), .pin9(n74161_1_pin9));
  Multiplexer #(.width(30)) multiplexer_1 (
    .in0(ADDR[31:2]), .in1(30'h3ffffffc),
    .out({multiplexer_1_out[29:12], n74161_6_pin3, multiplexer_1_out[7:0]}), .sel(or_1_out));
  Register #(.trigger("high"), .width(32)) register_1 (.D({PC[31:2], 2'b00}), .clk(1'b1));  // open: en, Q, clr
  or or_1 (or_1_out, INT, RST);
  _74161 #(.ShowInternalStructure("true")) u_74161_8 (
    .pin1(n74161_8_pin1), .pin2(CLK), .pin3(multiplexer_1_out[0]), .pin4(multiplexer_1_out[1]),
    .pin5(multiplexer_1_out[2]), .pin6(multiplexer_1_out[3]), .pin7(n74161_8_pin7), .pin15(n74161_7_pin10),
    .pin14(PC[2]), .pin13(PC[3]), .pin12(PC[4]), .pin11(PC[5]), .pin10(PCE), .pin9(n74161_1_pin9));
  or or_2 (EALIGN, ADDR[1], ADDR[0]);
  nor nor_1 (n74161_1_pin9, RST, INT, JMP);

  assign PC[1:0] = 2'b00;
  // also tied to GND on the sheet: {n74161_1_pin5, n74161_1_pin6}
  // also tied to VCC on the sheet: {n74161_1_pin1, n74161_1_pin7, n74161_2_pin7, n74161_3_pin1, n74161_3_pin7, n74161_4_pin1, n74161_4_pin7, n74161_5_pin1, n74161_5_pin7, n74161_6_pin1, n74161_6_pin7, n74161_7_pin1, n74161_7_pin7, n74161_8_pin1, n74161_8_pin7}
endmodule

module InstructionDecoder (
  input  [31:0] INSTR,
  output SIGILL,
  output [31:0] IMM
);

  wire nand_1_out, S4_1_0, S4_1_1, S10_5, S19_12, S30_20;
  wire [0:0] plarom_1_p3;
  wire [3:0] and_1_out, and_2_out;
  wire [5:0] plarom_2_p3;

  Register #(.trigger("high"), .width(32)) register_1 (.D(INSTR), .clk(1'b1));  // open: en, Q, clr
  nand nand_1 (nand_1_out, INSTR[0], INSTR[1]);
  LED led_1 (.in(INSTR[6]));
  LED led_2 (.in(INSTR[5]));
  LED led_3 (.in(INSTR[4]));
  LED led_4 (.in(INSTR[3]));
  LED led_5 (.in(INSTR[11]));
  LED led_6 (.in(INSTR[10]));
  LED led_7 (.in(INSTR[9]));
  LED led_8 (.in(INSTR[8]));
  LED led_9 (.in(INSTR[14]));
  LED led_10 (.in(INSTR[13]));
  LED led_11 (.in(INSTR[12]));
  LED led_12 (.in(INSTR[19]));
  LED led_13 (.in(INSTR[18]));
  LED led_14 (.in(INSTR[17]));
  LED led_15 (.in(INSTR[16]));
  LED led_16 (.in(INSTR[24]));
  LED led_17 (.in(INSTR[23]));
  LED led_18 (.in(INSTR[22]));
  LED led_19 (.in(INSTR[21]));
  LED led_20 (.in(INSTR[31]));
  LED led_21 (.in(INSTR[30]));
  LED led_22 (.in(INSTR[29]));
  LED led_23 (.in(INSTR[28]));
  LED led_24 (.in(INSTR[2]));
  LED led_25 (.in(INSTR[7]));
  LED led_26 (.in(INSTR[15]));
  LED led_27 (.in(INSTR[20]));
  LED led_28 (.in(INSTR[27]));
  LED led_29 (.in(INSTR[26]));
  LED led_30 (.in(INSTR[25]));
  // PlaRom #(.Contents("0 0 2 1 2 1*3 0 2 0 2*3 1 1 0 2 0 2 2 1 1 2 0 2 0 1*3 2 2 0 2 0 1 1 0 1 1 0*3 2*3 1 1 0*3 2 2 1 0 2 0*3 1*3 2 2 0*3 1 1 0 1 1 0*4 2 1*3 0*3 2 0*8 1 0 0 1 0*5 1 0*8 2 0*3 2*3 1*3 0 2 0 2 2 1 2*3 0 0 2 0*4 2 0*3 1 0 0 1 2 0*4 1 0 0 2 0*5 2 0*4 1 0 2 1 2 0*3 2 2 1 2*3 0*3 1 0*3 2 0*6 2 0*3 2 1 0*6 2 0 2 0 2 0*3 1 2 1 0 2 0*3 1 0 1 1 2 0*5 2 2 0*7 2 1 1 0*8 1 0*8 1 0*8 1 0*8 1 0*9 1 0*8 1 0*8 1 0*8 1 0*9 1 0*9 1 0*8 1 0*8 1 0*8 1 0*9 1 0*8 1 0*8 1 0 0 1 0*5 1 0*8 1 0 0 1 0*5 1 0 0 1 0*6 1 1 0*7 1 0*10 1 0*8 1 0*9 1 0*8 1 0*8 1 0*8 1 0*8 1 0*8 1"), .\and (30), .outputs(9)) plarom_1: pin names not known; wires that end beside it: {INSTR[31], INSTR[20], INSTR[7:2]}, 1'b0, {IMM[0], S4_1_0, S4_1_1, S10_5, IMM[11], S19_12, S30_20, IMM[31], plarom_1_p3[0]}
  // PlaRom #(.Contents("1 2 2 1*4 0 1*5 2*4 1 1 2*4 1*3 2 1*3 2 2 1*4 0 2 1 2*3 1 2*3 1 0*3 2 0 2 0 2 1 2 1 0 2 1 0 1 1 2 0 0 2 2 0*4 2 1 1 0*6 1 0*5 1 0*5 1 0*5 1 0*6 1 0*6 1 0*6 1 0*6 1 0*36"), .\and (15), .outputs(6)) plarom_2: pin names not known; wires that end beside it: INSTR[6:2], 1'b0, plarom_2_p3
  LED J (.in(plarom_2_p3[0]));
  LED U (.in(plarom_2_p3[1]));
  LED B (.in(plarom_2_p3[2]));
  LED S (.in(plarom_2_p3[3]));
  LED I (.in(plarom_2_p3[4]));
  LED R (.in(plarom_2_p3[5]));
  or or_1 (SIGILL, nand_1_out, plarom_1_p3[0]);
  assign and_1_out = {4{S4_1_1}} & INSTR[11:8];  // AND_Gate and_1, 4 bits wide
  assign IMM[4:1] = and_1_out | and_2_out;  // OR_Gate or_2, 4 bits wide
  assign and_2_out = {4{S4_1_0}} & INSTR[24:21];  // AND_Gate and_2, 4 bits wide
  assign IMM[10:5] = {6{S10_5}} & INSTR[30:25];  // AND_Gate and_3, 6 bits wide
  Multiplexer #(.width(8)) multiplexer_1 (.in0({8{IMM[31]}}), .in1(INSTR[19:12]), .out(IMM[19:12]), .sel(S19_12));
  Multiplexer #(.width(11)) multiplexer_2 (.in0({11{IMM[31]}}), .in1(INSTR[30:20]), .out(IMM[30:20]), .sel(S30_20));

  // Other names for the same wires on the sheet: OP[4:0] = INSTR[6:2]; P7 = INSTR[7]; P31 = INSTR[31];
  //   P20 = INSTR[20]; P24_20[4:0] = INSTR[24:20]; P24_21[3:0] = INSTR[24:21]; P30_25[5:0] = INSTR[30:25];
  //   X0 = IMM[0]; X11 = IMM[11]; X31 = IMM[31]; P11_8[3:0] = INSTR[11:8]; P19_12[7:0] = INSTR[19:12]

  // Notes on the sheet:
  //   2'b11
  //   OP
  //   rd/imm
  //   funct3/imm
  //   rs1/imm
  //   rs2/imm
  //   funct7/imm
  //   ILL
  //   X31
  //   S[30:20]
  //   S[19:12]
  //   X11
  //   S[10:5]
  //   S[4:1].1
  //   S[4:1].0
  //   X0
endmodule

module ArithmeticLogicUnit (
  input  CLK,
  input  [31:0] X,
  input  [31:0] Y,
  input  [3:0] SEL,
  output RDY,
  output EQ,
  output LT,
  output GT,
  output LTU,
  output GTU,
  output [31:0] R
);

  wire decoder_1_out0, decoder_1_out1, decoder_1_out2, decoder_1_out3, decoder_1_out4, decoder_1_out5,
       decoder_1_out6, decoder_1_out7, decoder_1_out8, decoder_1_out9, decoder_1_out10, decoder_1_out11,
       decoder_1_out12, decoder_1_out13, decoder_1_out14, decoder_1_out15, OVF;
  wire [31:0] ANDV, DIFF, ORV, SARV, shifter_1_out, shifter_2_out, shifter_3_out, SHLV, SHRV, SPRODH, SPRODL,
       SQUOT, SREM, SUM, UPRODH, UPRODL, UQUOT, UREM, XORV;

  Adder #(.width(32)) adder_1 (.a(X), .b(Y), .out(SUM));  // open: cin, cout
  Subtractor #(.width(32)) subtractor_1 (.a(X), .b(Y), .out(DIFF));  // open: bin, bout
  Multiplier #(.mode("twosComplement"), .width(32)) multiplier_1 (
    .a(X), .b(Y), .out(SPRODL), .cout(SPRODH));  // open: cin
  Multiplier #(.width(32)) multiplier_2 (.a(X), .b(Y), .out(UPRODL), .cout(UPRODH));  // open: cin
  Divider #(.mode("twosComplement"), .width(32)) divider_1 (.a(X), .b(Y), .out(SQUOT), .rem(SREM));  // open: upper
  Divider #(.width(32)) divider_2 (.a(X), .b(Y), .out(UQUOT), .rem(UREM));  // open: upper
  Register #(.trigger("high"), .width(32)) u_SUM (.D(SUM), .clk(1'b1));  // open: en, Q, clr
  Register #(.trigger("high"), .width(32)) u_DIFF (.D(DIFF), .clk(1'b1));  // open: en, Q, clr
  Register #(.trigger("high"), .width(32)) u_SPRODL (.D(SPRODL), .clk(1'b1));  // open: en, Q, clr
  Register #(.trigger("high"), .width(32)) u_SPRODH (.D(SPRODH), .clk(1'b1));  // open: en, Q, clr
  Register #(.trigger("high"), .width(32)) u_UPRODL (.D(UPRODL), .clk(1'b1));  // open: en, Q, clr
  Register #(.trigger("high"), .width(32)) u_UPRODH (.D(UPRODH), .clk(1'b1));  // open: en, Q, clr
  Register #(.trigger("high"), .width(32)) u_SQUOT (.D(SQUOT), .clk(1'b1));  // open: en, Q, clr
  Register #(.trigger("high"), .width(32)) u_SREM (.D(SREM), .clk(1'b1));  // open: en, Q, clr
  Register #(.trigger("high"), .width(32)) u_UQUOT (.D(UQUOT), .clk(1'b1));  // open: en, Q, clr
  Register #(.trigger("high"), .width(32)) u_UREM (.D(UREM), .clk(1'b1));  // open: en, Q, clr
  assign ORV = X | Y;  // OR_Gate or_1, 32 bits wide
  assign ANDV = X & Y;  // AND_Gate and_1, 32 bits wide
  assign XORV = X ^ Y;  // XOR_Gate xor_1, 32 bits wide
  Shifter #(.width(32)) shifter_1 (.in(X), .\dist (Y[4:0]), .out(shifter_1_out));
  Shifter #(.shift("lr"), .width(32)) shifter_2 (.in(X), .\dist (Y[4:0]), .out(shifter_2_out));
  Shifter #(.shift("ar"), .width(32)) shifter_3 (.in(X), .\dist (Y[4:0]), .out(shifter_3_out));
  Comparator #(.width(32)) comparator_1 (.a(X), .b(Y), .gt(GT), .eq(EQ), .lt(LT));
  Comparator #(.mode("unsigned"), .width(32)) comparator_2 (.a(X), .b(Y), .gt(GTU), .lt(LTU));  // open: eq
  Multiplexer #(.width(32)) multiplexer_1 (.in0(shifter_1_out), .in1({32{1'b0}}), .out(SHLV), .sel(OVF));
  Multiplexer #(.width(32)) multiplexer_2 (.in0(shifter_2_out), .in1({32{1'b0}}), .out(SHRV), .sel(OVF));
  Multiplexer #(.width(32)) multiplexer_3 (.in0(shifter_3_out), .in1({32{1'b0}}), .out(SARV), .sel(OVF));
  Register #(.trigger("high"), .width(32)) u_ORV (.D(ORV), .clk(1'b1));  // open: en, Q, clr
  Register #(.trigger("high"), .width(32)) u_ANDV (.D(ANDV), .clk(1'b1));  // open: en, Q, clr
  Register #(.trigger("high"), .width(32)) u_XORV (.D(XORV), .clk(1'b1));  // open: en, Q, clr
  Register #(.trigger("high"), .width(32)) u_SHLV (.D(SHLV), .clk(1'b1));  // open: en, Q, clr
  Register #(.trigger("high"), .width(32)) u_SHRV (.D(SHRV), .clk(1'b1));  // open: en, Q, clr
  Register #(.trigger("high"), .width(32)) u_SARV (.D(SARV), .clk(1'b1));  // open: en, Q, clr
  LED F_SUM (.in(decoder_1_out0));
  LED F_DIFF (.in(decoder_1_out1));
  LED F_SPRODL (.in(decoder_1_out2));
  LED F_SPRODH (.in(decoder_1_out3));
  LED F_UPRODL (.in(decoder_1_out4));
  LED F_UPRODH (.in(decoder_1_out5));
  LED F_SQUOT (.in(decoder_1_out6));
  LED F_SREM (.in(decoder_1_out7));
  LED F_UQUOT (.in(decoder_1_out8));
  LED F_UREM (.in(decoder_1_out9));
  LED F_ORV (.in(decoder_1_out10));
  LED F_ANDV (.in(decoder_1_out11));
  LED F_XORV (.in(decoder_1_out12));
  LED F_SHLV (.in(decoder_1_out13));
  LED F_SHRV (.in(decoder_1_out14));
  LED F_SARV (.in(decoder_1_out15));
  Multiplexer #(.select(4), .width(32)) multiplexer_4 (
    .in0(SUM), .in1(DIFF), .in2(SPRODL), .in3(SPRODH), .in4(UPRODL), .in5(UPRODH), .in6(SQUOT), .in7(SREM),
    .in8(UQUOT), .in9(UREM), .in10(ORV), .in11(ANDV), .in12(XORV), .in13(SHLV), .in14(SHRV), .in15(SARV),
    .out(R), .sel(SEL));
  Decoder #(.select(4)) decoder_1 (
    .out0(decoder_1_out0), .out1(decoder_1_out1), .out2(decoder_1_out2), .out3(decoder_1_out3),
    .out4(decoder_1_out4), .out5(decoder_1_out5), .out6(decoder_1_out6), .out7(decoder_1_out7),
    .out8(decoder_1_out8), .out9(decoder_1_out9), .out10(decoder_1_out10), .out11(decoder_1_out11),
    .out12(decoder_1_out12), .out13(decoder_1_out13), .out14(decoder_1_out14), .out15(decoder_1_out15),
    .sel(SEL), .en(1'b1));
  LED C_EQ (.in(EQ));
  LED C_LT (.in(LT));
  LED C_GT (.in(GT));
  LED C_LTU (.in(LTU));
  LED C_GTU (.in(GTU));
  or or_2 (OVF, Y[5], Y[6], Y[7], Y[8], Y[9], Y[10], Y[11], Y[12], Y[13], Y[14], Y[15], Y[16], Y[17], Y[18], Y[19], Y[20], Y[21], Y[22], Y[23], Y[24], Y[25], Y[26], Y[27], Y[28], Y[29], Y[30], Y[31]);

  assign RDY = 1'b1;

  // Other names for the same wires on the sheet: Y4_0[4:0] = Y[4:0]
endmodule

module LoadStoreUnit (
  input  nBUSY,
  input  CLK,
  input  RST,
  input  [31:0] DOUT,
  input  FETCH,
  input  LOAD0,
  input  LOAD1,
  input  STORE0,
  input  [31:0] DI,
  input  STORE1,
  input  [31:0] ADDR,
  input  [31:0] PC,
  output [31:0] DO,
  output STROBE,
  output RDY,
  output EALIGN,
  output BM0,
  output BM1,
  output BM2,
  output BM3,
  output [31:0] INSTR,
  output nRW,
  output PCE,
  output [31:0] DIN,
  output [29:0] A
);

  wire and_9_out, d_ff_1_q, IO, nor_1_out, not_1_out, not_2_out, not_3_out, or_1_out, S0, S1, S2, S3;
  wire [1:0] multiplexer_2_out;
  wire [7:0] and_1_out, and_2_out, and_3_out, and_4_out, and_5_out, and_6_out, and_7_out, and_8_out,
       bit_extender_1_out, bit_extender_2_out, bit_extender_3_out, bit_extender_4_out, bit_extender_5_out,
       bit_extender_6_out, bit_extender_7_out, bit_extender_8_out;
  wire [31:0] controlled_buffer_1_out, shifter_1_out, shifter_2_out, shifter_3_out, shifter_4_out,
       shifter_5_out, shifter_6_out;

  Register #(.trigger("high"), .width(32)) MDR (.D(DI), .clk(1'b1));  // open: en, Q, clr
  assign controlled_buffer_1_out = S0 ? DOUT : 32'bz;  // Controlled_Buffer controlled_buffer_1
  assign controlled_buffer_1_out = S1 ? shifter_1_out : 32'bz;  // Controlled_Buffer controlled_buffer_2
  Shifter #(.width(32)) shifter_1 (.in(DOUT), .\dist (5'b01000), .out(shifter_1_out));
  assign controlled_buffer_1_out = S2 ? shifter_2_out : 32'bz;  // Controlled_Buffer controlled_buffer_3
  Shifter #(.width(32)) shifter_2 (.in(DOUT), .\dist (5'b10000), .out(shifter_2_out));
  assign controlled_buffer_1_out = S3 ? shifter_3_out : 32'bz;  // Controlled_Buffer controlled_buffer_4
  Shifter #(.width(32)) shifter_3 (.in(DOUT), .\dist (5'b11000), .out(shifter_3_out));
  assign and_1_out = DI[7:0] & bit_extender_1_out;  // AND_Gate and_1, 8 bits wide
  assign bit_extender_1_out = {{7{BM0}}, BM0};  // Bit_Extender bit_extender_1
  assign and_2_out = DI[15:8] & bit_extender_2_out;  // AND_Gate and_2, 8 bits wide
  assign bit_extender_2_out = {{7{BM1}}, BM1};  // Bit_Extender bit_extender_2
  assign and_3_out = DI[23:16] & bit_extender_3_out;  // AND_Gate and_3, 8 bits wide
  assign bit_extender_3_out = {{7{BM2}}, BM2};  // Bit_Extender bit_extender_3
  assign and_4_out = DI[31:24] & bit_extender_4_out;  // AND_Gate and_4, 8 bits wide
  assign bit_extender_4_out = {{7{BM3}}, BM3};  // Bit_Extender bit_extender_4
  assign and_5_out = controlled_buffer_1_out[7:0] & bit_extender_5_out;  // AND_Gate and_5, 8 bits wide
  assign bit_extender_5_out = {{7{BM0}}, BM0};  // Bit_Extender bit_extender_5
  assign and_6_out = controlled_buffer_1_out[15:8] & bit_extender_6_out;  // AND_Gate and_6, 8 bits wide
  assign bit_extender_6_out = {{7{BM1}}, BM1};  // Bit_Extender bit_extender_6
  assign and_7_out = controlled_buffer_1_out[23:16] & bit_extender_7_out;  // AND_Gate and_7, 8 bits wide
  assign bit_extender_7_out = {{7{BM2}}, BM2};  // Bit_Extender bit_extender_7
  assign and_8_out = controlled_buffer_1_out[31:24] & bit_extender_8_out;  // AND_Gate and_8, 8 bits wide
  assign bit_extender_8_out = {{7{BM3}}, BM3};  // Bit_Extender bit_extender_8
  assign DIN = S0 ? {and_4_out, and_3_out, and_2_out, and_1_out} : 32'bz;  // Controlled_Buffer controlled_buffer_5
  assign DIN = S1 ? shifter_4_out : 32'bz;  // Controlled_Buffer controlled_buffer_6
  Shifter #(.shift("lr"), .width(32)) shifter_4 (
    .in({and_4_out, and_3_out, and_2_out, and_1_out}), .\dist (5'b01000), .out(shifter_4_out));
  assign DIN = S2 ? shifter_5_out : 32'bz;  // Controlled_Buffer controlled_buffer_7
  Shifter #(.shift("lr"), .width(32)) shifter_5 (
    .in({and_4_out, and_3_out, and_2_out, and_1_out}), .\dist (5'b10000), .out(shifter_5_out));
  assign DIN = S3 ? shifter_6_out : 32'bz;  // Controlled_Buffer controlled_buffer_8
  Shifter #(.shift("lr"), .width(32)) shifter_6 (
    .in({and_4_out, and_3_out, and_2_out, and_1_out}), .\dist (5'b11000), .out(shifter_6_out));
  assign DO = nRW ? {and_8_out, and_7_out, and_6_out, and_5_out} : 32'bz;  // Controlled_Buffer controlled_buffer_9
  not not_1 (not_1_out, RST);
  and and_9 (and_9_out, not_1_out, PCE);
  Multiplexer #(.width(32)) multiplexer_1 (.in0(32'h13), .in1(DIN), .out(INSTR), .sel(and_9_out));
  D_Flip_Flop d_ff_1 (.D(not_2_out), .clk(CLK), .Q(d_ff_1_q), .Qn(RDY), .reset(RST));  // open: preset
  not not_2 (not_2_out, nBUSY);
  nor nor_1 (nor_1_out, LOAD0, LOAD1, STORE0, STORE1);
  and and_10 (PCE, FETCH, nor_1_out);
  Multiplexer #(.width(32)) multiplexer_2 (.in0(ADDR), .in1(PC), .out({A, multiplexer_2_out}), .sel(nor_1_out));
  not not_3 (not_3_out, RST);
  // PlaRom #(.Contents("0*6 2 0*5 2 0*5 2 0*5 2 0*5 2 0*4 1 1 0 0 2 2 0 1 1 2 0 0 2 0 1 1 0 2 2 0 0 1 1 2 2 0*3 2 2 1 0 1 2 0 2 2 1 2 1 0 0 2 1 0 1 2 1 0 2 1 2 1 0 1 0 1*6 2 2 1 1 0 1 2 0 2 1 1 2 1 0 0 1 1 0 0 2 0 0 1 1 2 0*4 1 2 1 0 1 2 0 1 2 1 2 1 0 0 1 1 0 1 0 1 2 1 1 0*4 2 1 1 0*3 2 0 1 1 0 2 0*4 2 0 0 2 0*3 2 2 0*4 2 0*3 2 2 0 2 0 2 0 0 2 0 2 0 0 2 2 0 0 2 0 2 2 0*4 2 0 1 0 1 2 2 0 1*4 2 1 0*6 1 0*6 1 0*6 1 1 0*5 1 1 0*7 1 1 0*5 1 1 0*5 1 1 0*5 1 1 0*5 1 0*6 1 0*6 1 1 0*5 1 1 0*5 1 1 0*6 1 0*6 1 0*7 1 1 0*5 1 1 0*5 1 0*6 1 0*6 1 0*7 1 0*6 1 0*6 1 0*7 1 0*6 1 0*6 1 0*6 1 0*6 1 0*6 1 0*6 1 0*6 1"), .\and (32), .outputs(7)) MaskGen: pin names not known; wires that end beside it: {multiplexer_2_out, STORE1, STORE0, LOAD1, LOAD0, FETCH}, 1'b0, {IO, nRW, BM3, BM2, BM1, BM0, EALIGN}
  Register #(.trigger("high"), .width(32)) MAR (.D({A, multiplexer_2_out}), .clk(1'b1));  // open: en, Q, clr
  or or_1 (or_1_out, CLK, d_ff_1_q);
  and and_11 (STROBE, IO, or_1_out, not_3_out);
  Decoder #(.enable("false"), .select(2)) decoder_1 (
    .out0(S0), .out1(S1), .out2(S2), .out3(S3), .sel(multiplexer_2_out));

  // Other names for the same wires on the sheet: M0 = BM0; M1 = BM1; M2 = BM2; M3 = BM3; ST = nRW

  // Notes on the sheet:
  //   nBUSY: pull=up
  //   RST: pull=up
endmodule
